// Logisim project My-Triggers.circ as structural Verilog: 1 circuit, main circuit main
module main (
);

  wire and_1_out, and_2_out, and_3_out, and_4_out, and_5_out, and_6_out, and_7_out, and_8_out, button_1_out,
       button_2_out, D1, D2, D3, nor_1_out, nor_3_out, not_1_out, not_2_out, not_3_out, not_4_out, not_5_out,
       not_6_out, t_ff_1_q, t_ff_2_q, t_ff_3_q, t_ff_3_qn, t_ff_4_q;
  wire [2:0] t_ff_1_qn;
  wire [3:0] d_ff_1_q;

  Button button_1 (.out(button_1_out));
  Button button_2 (.out(button_2_out));
  Hex_Digit_Display hex_digit_display_1 (.value(d_ff_1_q));  // open: dp
  T_Flip_Flop #(.trigger("falling")) t_ff_1 (
    .clk(button_2_out), .T(1'b1), .Q(t_ff_1_q), .Qn(t_ff_1_qn[0]), .reset(and_5_out));  // open: preset, en
  D_Flip_Flop #(.trigger("falling")) d_ff_1 (
    .clk(button_1_out), .D(1'b0), .Q(d_ff_1_q[0]));  // open: Qn, preset, en, reset
  T_Flip_Flop #(.trigger("falling")) t_ff_2 (
    .clk(t_ff_1_q), .T(1'b1), .Q(t_ff_2_q), .reset(and_5_out));  // open: Qn, preset, en
  D_Flip_Flop #(.trigger("falling")) d_ff_2 (
    .clk(button_1_out), .D(D1), .Q(d_ff_1_q[1]));  // open: Qn, preset, en, reset
  nor nor_1 (nor_1_out, d_ff_1_q[0], d_ff_1_q[1], d_ff_1_q[2]);
  not not_1 (not_1_out, d_ff_1_q[0]);
  not not_2 (not_2_out, d_ff_1_q[1]);
  and and_1 (and_1_out, not_1_out, not_2_out, d_ff_1_q[2], not_3_out);
  not not_3 (not_3_out, d_ff_1_q[3]);
  not not_4 (not_4_out, d_ff_1_q[0]);
  and and_2 (and_2_out, not_4_out, d_ff_1_q[1], d_ff_1_q[2], not_5_out);
  not not_5 (not_5_out, d_ff_1_q[3]);
  nor nor_2 (D3, d_ff_1_q[0], d_ff_1_q[1], d_ff_1_q[2], d_ff_1_q[3]);
  T_Flip_Flop #(.trigger("falling")) t_ff_3 (
    .clk(t_ff_2_q), .T(1'b1), .Q(t_ff_3_q), .Qn(t_ff_3_qn), .reset(and_5_out));  // open: preset, en
  and and_3 (and_3_out, nor_1_out, d_ff_1_q[3]);
  or or_1 (D1, and_3_out, and_1_out);
  or or_2 (D2, and_2_out, and_3_out);
  D_Flip_Flop #(.trigger("falling")) d_ff_3 (
    .clk(button_1_out), .D(D2), .Q(d_ff_1_q[2]));  // open: Qn, preset, en, reset
  T_Flip_Flop #(.trigger("falling")) t_ff_4 (
    .clk(t_ff_3_q), .T(1'b1), .Q(t_ff_4_q), .reset(and_5_out));  // open: Qn, preset, en
  D_Flip_Flop #(.trigger("falling")) d_ff_4 (
    .clk(button_1_out), .D(D3), .Q(d_ff_1_q[3]));  // open: Qn, preset, en, reset
  or or_3 (t_ff_1_qn[2], nor_3_out, and_4_out);
  nor nor_3 (nor_3_out, t_ff_2_q, t_ff_3_q, t_ff_4_q);
  not not_6 (not_6_out, button_2_out);
  and and_4 (and_4_out, t_ff_1_q, t_ff_4_q);
  and and_5 (and_5_out, not_6_out, t_ff_1_qn[0], t_ff_2_q, t_ff_3_qn, t_ff_4_q);
  Hex_Digit_Display hex_digit_display_2 (.value({1'b0, t_ff_1_qn}));  // open: dp
  and and_6 (and_6_out, t_ff_1_qn[0], t_ff_4_q);
  and and_7 (and_7_out, t_ff_2_q, t_ff_3_qn);
  and and_8 (and_8_out, t_ff_1_q, t_ff_2_q);
  or or_4 (t_ff_1_qn[1], and_6_out, and_7_out, and_8_out);
endmodule
