// Logisim project Triggers.circ as structural Verilog: 1 circuit, main circuit main
module main (
  input  S,
  input  Not_S,
  input  R,
  input  C,
  input  Not_R,
  input  S_2,
  input  R_2,
  input  Not_S_2,
  input  D,
  input  S_3,
  input  C_2,
  input  C_3,
  input  R_3,
  input  Not_R_2,
  input  Not_S_3,
  input  Not_S_4,
  input  Not_R_3,
  input  Not_R_4,
  input  Not_S_5,
  input  Not_S_6,
  input  J,
  input  T,
  input  C_4,
  input  K,
  input  Not_R_5,
  input  Not_R_6,
  input  in_27,
  input  D_2,
  input  C_5,
  input  T_2
);

  wire nand_1_out, nand_2_out, nand_3_out, nand_4_out, nand_5_out, nand_6_out, nand_7_out, nand_8_out,
       nand_9_out, nand_10_out, nand_11_out, nand_12_out, nand_13_out, nand_14_out, nand_15_out, nand_16_out,
       nand_17_out, nand_18_out, nand_19_out, nand_20_out, nand_21_out, nand_22_out, nand_23_out,
       nand_24_out, nand_25_out, nand_26_out, nand_27_out, nand_28_out, nand_29_out, nand_30_out,
       nand_31_out, nand_32_out, nand_33_out, nand_34_out, nand_35_out, nand_36_out, nand_37_out,
       nand_38_out, nand_39_out, nand_40_out, nand_41_out, nand_42_out, nand_43_out, nand_44_out,
       nand_45_out, nand_46_out, nand_47_out, nand_48_out, nand_49_out, nand_50_out, nand_51_out,
       nand_52_out, nand_53_out, nand_54_out, nand_55_out, nand_56_out, nand_57_out, nor_1_out, nor_2_out,
       nor_3_out, nor_4_out, nor_5_out, nor_6_out, nor_7_out, nor_8_out, \С_2_out , \С_out ;

  Clock \u_С  (.out(\С_out ));
  nand nand_1 (nand_1_out, nand_2_out, Not_S);
  nand nand_2 (nand_2_out, Not_R, nand_1_out);
  nand nand_3 (nand_3_out, C_3, C_3);
  nand nand_4 (nand_4_out, Not_S_3, nand_11_out);
  nand nand_5 (nand_5_out, nand_12_out, Not_R_3);
  nand nand_6 (nand_6_out, T, T);
  nand nand_7 (nand_7_out, nand_35_out, in_27, T_2);
  nand nand_8 (nand_8_out, T_2, nand_7_out);
  nand nand_9 (nand_9_out, S_3, nand_3_out);
  nand nand_10 (nand_10_out, nand_3_out, R_3);
  nand nand_11 (nand_11_out, nand_12_out, nand_4_out, \С_out );
  nand nand_12 (nand_12_out, \С_out , nand_5_out, nand_11_out);
  nand nand_13 (nand_13_out, nand_31_out, nand_6_out);
  nand nand_14 (nand_14_out, nand_6_out, nand_30_out);
  nand nand_15 (nand_15_out, nand_7_out, nand_16_out);
  nand nand_16 (nand_16_out, nand_15_out, nand_8_out);
  // Probe on nand_1_out
  // Probe on nand_2_out
  nand nand_17 (nand_17_out, Not_S_2, nand_9_out, nand_18_out);
  nand nand_18 (nand_18_out, nand_17_out, nand_10_out, Not_R_2);
  nand nand_19 (nand_19_out, Not_S_5, nand_13_out, nand_20_out);
  nand nand_20 (nand_20_out, nand_19_out, nand_14_out, Not_R_5);
  nand nand_21 (nand_21_out, nand_17_out, C_3);
  nand nand_22 (nand_22_out, C_3, nand_18_out);
  nand nand_23 (nand_23_out, nand_11_out, nand_24_out);
  nand nand_24 (nand_24_out, nand_23_out, nand_12_out);
  nand nand_25 (nand_25_out, nand_19_out, T);
  nand nand_26 (nand_26_out, T, nand_20_out);
  nand nand_27 (nand_27_out, T_2, T_2);
  nor nor_1 (nor_1_out, nor_2_out, R);
  nor nor_2 (nor_2_out, S_2, nor_1_out);
  nand nand_28 (nand_28_out, Not_S_2, nand_21_out, nand_29_out);
  nand nand_29 (nand_29_out, nand_28_out, nand_22_out, Not_R_2);
  nand nand_30 (nand_30_out, Not_S_5, nand_25_out, nand_31_out);
  nand nand_31 (nand_31_out, nand_30_out, nand_26_out, Not_R_5);
  nand nand_32 (nand_32_out, nand_15_out, in_27, nand_27_out);
  nand nand_33 (nand_33_out, nand_27_out, nand_32_out);
  // Probe on nand_23_out
  // Probe on nand_24_out
  nand nand_34 (nand_34_out, nand_32_out, nand_35_out);
  nand nand_35 (nand_35_out, nand_34_out, nand_33_out);
  // Probe on nor_1_out
  // Probe on nor_2_out
  // Probe on nand_28_out
  // Probe on nand_29_out
  // Probe on nand_30_out
  // Probe on nand_31_out
  // Probe on nand_34_out
  // Probe on nand_35_out
  Clock \u_С_2  (.out(\С_2_out ));
  nand nand_36 (nand_36_out, S, C);
  nand nand_37 (nand_37_out, C, R_2);
  nand nand_38 (nand_38_out, D, C_2);
  nand nand_39 (nand_39_out, C_2, nand_40_out);
  nand nand_40 (nand_40_out, D, D);
  nor nor_3 (nor_3_out, Not_S_4, nor_5_out);
  nor nor_4 (nor_4_out, nor_6_out, Not_R_4);
  nand nand_41 (nand_41_out, C_4, C_4);
  nand nand_42 (nand_42_out, nand_36_out, nand_43_out);
  nand nand_43 (nand_43_out, nand_42_out, nand_37_out);
  nand nand_44 (nand_44_out, nand_45_out, nand_38_out);
  nand nand_45 (nand_45_out, nand_39_out, nand_44_out);
  nor nor_5 (nor_5_out, nor_6_out, nor_3_out, \С_2_out );
  nor nor_6 (nor_6_out, \С_2_out , nor_4_out, nor_5_out);
  nand nand_46 (nand_46_out, nand_57_out, J, nand_41_out);
  nand nand_47 (nand_47_out, nand_41_out, K, nand_56_out);
  // Probe on nand_42_out
  // Probe on nand_43_out
  // Probe on nand_44_out
  // Probe on nand_45_out
  nand nand_48 (nand_48_out, Not_S_6, nand_46_out, nand_49_out);
  nand nand_49 (nand_49_out, nand_48_out, nand_47_out, Not_R_6);
  nand nand_50 (nand_50_out, D_2, C_5);
  nand nand_51 (nand_51_out, C_5, nand_50_out);
  nand nand_52 (nand_52_out, nand_50_out, nand_53_out);
  nand nand_53 (nand_53_out, nand_52_out, nand_51_out);
  nor nor_7 (nor_7_out, nor_5_out, nor_8_out);
  nor nor_8 (nor_8_out, nor_7_out, nor_6_out);
  nand nand_54 (nand_54_out, nand_48_out, C_4);
  nand nand_55 (nand_55_out, C_4, nand_49_out);
  // Probe on nand_52_out
  // Probe on nand_53_out
  // Probe on nor_7_out
  // Probe on nor_8_out
  nand nand_56 (nand_56_out, Not_S_6, nand_54_out, nand_57_out);
  nand nand_57 (nand_57_out, nand_56_out, nand_55_out, Not_R_6);
  // Probe on nand_56_out
  // Probe on nand_57_out
endmodule
